# Fritzing sketch NE555 LED Blinker (saved by Fritzing 1.0.5)
circuit board: 8.46667cm x 5.64444cm
breadboards: 1

parts:
  IC1 = General purpose bipolar Timer [package=dil-08]
  C1 = Electrolytic Capacitor [capacitance=10μF voltage=50V package="0605 [SMD, electrolytic]"]
  LED1 = smd LED [color="Red (633nm)" package="1206 [SMD]"]
  R1 = Resistor [tolerance=±5% resistance=4.7k package="0603 [SMD]"]
  R2 = Resistor [tolerance=±5% resistance=4.7k package="0603 [SMD]"]
  BAT1 = BC9VPC [package=bc9vpc]

nets:
  N1: IC1.GND, C1.-, LED1.cathode, BAT1.V-
  N2: IC1.TRI, IC1.TRE, C1.+, R1.Pin_0
  N3: IC1.OUT, LED1.anode
  N4: IC1._RES, IC1.VCC+, R2.Pin_1, BAT1.V+
  N5: IC1.DIS, R1.Pin_1, R2.Pin_0
