# Fritzing sketch led-flashlight (saved by Fritzing 1.0.5)
breadboards: 1

parts:
  R1 = Resistor [tolerance=±5% resistance=220 package="1206 [SMD]"]
  R2 = Resistor [tolerance=±5% resistance=220 package="1206 [SMD]"]
  R3 = Resistor [tolerance=±5% resistance=220 package="1206 [SMD]"]
  R4 = Resistor [tolerance=±5% resistance=220 package="1206 [SMD]"]
  R5 = Resistor [tolerance=±5% resistance=220 package="1206 [SMD]"]
  LED5 = LED - 5mm [color="Blue (430nm)" current=30mA package="5 mm [THT]"]
  S1 = SWITCH-MOMENTARY-2 [package=tactile-pth]
  BAT1 = BC9VPC [package=bc9vpc]
  LED6 = LED - 5mm [color="Green (565nm)" current=0.030A package="5 mm [THT]"]
  LED7 = LED - 5mm [color="Yellow (574nm)" current=0.030A package="5 mm [THT]"]
  LED8 = LED - 5mm [color="White (8000K)" current=0.030A package="5 mm [THT]"]
  LED9 = LED - 5mm [color="Red (633nm)" current=0.030A package="5 mm [THT]"]

nets:
  N1: R1.Pin_0, R2.Pin_0, R3.Pin_0, R4.Pin_0, S1.1, BAT1.V+
  N2: R1.Pin_1, LED5.anode
  N3: R2.Pin_1, LED6.anode
  N4: R3.Pin_1, LED7.anode
  N5: R4.Pin_1, LED9.anode
  N6: R5.Pin_1, LED8.anode
  N7: LED5.cathode, S1.2, BAT1.V-, LED6.cathode, LED7.cathode, LED8.cathode, LED9.cathode
