# Fritzing sketch dark-activated-led (saved by Fritzing 1.0.5)
breadboards: 1

parts:
  R1 = Resistor [tolerance=±5% resistance=220 package="0805 [SMD]"]
  2n3906 = PNP-Transistor [package="TO92 [THT]"]
  R2 = Resistor [tolerance=±5% resistance=1k package="0805 [SMD]"]
  R3 = Resistor [tolerance=±5% resistance=1k package="0805 [SMD]"]
  LED1 = LED - 3mm [color="Red (633nm)" current=0.030A package="3 mm [THT]"]
  LDR = Photocell (LDR) [power=0.25W dark_resistance_@0.01lx=40kΩ light_resistance_@100lx=400 luminance=10lx package=THT]
  VCC1 = Battery block 9V [internal_resistance=0.1Ω]

nets:
  N1: R1.Pin_0, LED1.anode
  N2: R1.Pin_1, LDR.pin_0, VCC1.+
  N3: 2n3906.E, R3.Pin_1, VCC1.-
  N4: 2n3906.B, R2.Pin_1
  N5: 2n3906.C, LED1.cathode
  N6: R2.Pin_0, R3.Pin_0, LDR.pin_1
