# Fritzing sketch push-button-debouncing (saved by Fritzing 1.0.5)
circuit board: 4.44742cm x 4.71058cm
breadboards: 1

parts:
  S1 = SWITCH-MOMENTARY-2 [package=tactile-pth]
  C1 = Electrolytic Capacitor [capacitance=10μF voltage=35V package="0605 [SMD, electrolytic]"]
  R1 = Resistor [tolerance=±5% power=0.25W resistance=220 package=THT]
  R2 = Resistor [tolerance=±5% power=0.25W resistance=10k package=THT]
  LED1 = LED - 5mm [color="Red (633nm)" current=0.030A package="5 mm [THT]"]
  VCC1 = Battery block 9V [internal_resistance=0.1Ω]

nets (from the schematic view):
  N1: S1.1, VCC1.+
  N2: S1.2, C1.+, R1.Pin_0
  N3: C1.-, R1.Pin_1, R2.Pin_0, LED1.anode, VCC1.-
  N4: R2.Pin_1, LED1.cathode
