# Fritzing sketch Audio Amplifier Stereo Speakers (saved by Fritzing 1.0.6)
breadboards: 1

parts:
  C1 = Electrolytic Capacitor [capacitance=10µF voltage=50V package="100 mil [THT, electrolytic]"]
  C2 = Electrolytic Capacitor [capacitance=220µF voltage=50V package="100 mil [THT, electrolytic]"]
  SP1 = SPEAKER [package=pcb_mount_speaker]
  VCC1 = Battery block 9V [internal_resistance=0.1Ω]
  TRS1 = Audio Jack (TRS) 3.5mm [package="PG203J [THT]"]
  U3 = LM386 [package=dip08]
  C5 = Ceramic Capacitor [capacitance="100 nF" voltage=35V package="1206 [SMD, multilayer]"]
  LED1 = smd LED [color="Red (633nm)" package="0805 [SMD]"]
  R1 = Resistor [tolerance=±5% resistance=220 package="2010 [SMD]"]
  C6 = Electrolytic Capacitor [capacitance=10µF voltage=50V package="100 mil [THT, electrolytic]"]
  C7 = Electrolytic Capacitor [capacitance=220µF voltage=50V package="100 mil [THT, electrolytic]"]
  SP2 = SPEAKER [package=pcb_mount_speaker]
  VCC2 = Battery block 9V [internal_resistance=0.1Ω]
  U4 = LM386 [package=dip08]
  C8 = Ceramic Capacitor [capacitance="100 nF" voltage=35V package="1206 [SMD, multilayer]"]
  LED2 = smd LED [color="Red (633nm)" package="0805 [SMD]"]
  R2 = Resistor [tolerance=±5% resistance=220 package="2010 [SMD]"]

nets:
  N1: C1.-, U3.+IN
  N2: C1.+, TRS1.Tip
  N3: C2.-, SP1.+
  N4: C2.+, U3.OUT
  N5: SP1.-, VCC1.-, TRS1.Sleeve, U3.-IN, U3.V-, C5.1, R1.Pin_1
  N6: VCC1.+, U3.V+, LED1.anode
  N7: TRS1.Ring, C6.+
  N8: U3.BP, C5.0
  N9: LED1.cathode, R1.Pin_0
  N10: C6.-, U4.+IN
  N11: C7.-, SP2.+
  N12: C7.+, U4.OUT
  N13: SP2.-, VCC2.-, U4.-IN, U4.V-, C8.1, R2.Pin_1
  N14: VCC2.+, U4.V+, LED2.anode
  N15: U4.BP, C8.0
  N16: LED2.cathode, R2.Pin_0
