# Fritzing sketch Audio Amplifier (saved by Fritzing 1.0.6)
breadboards: 1

parts:
  C1 = Electrolytic Capacitor [capacitance=10µF voltage=50V package="100 mil [THT, electrolytic]"]
  C2 = Electrolytic Capacitor [capacitance=220µF voltage=50V package="100 mil [THT, electrolytic]"]
  SP1 = SPEAKER [package=pcb_mount_speaker]
  VCC1 = Battery block 9V [internal_resistance=0.1Ω]
  TRS1 = Audio Jack (TRS) 3.5mm [package="PG203J [THT]"]
  U3 = LM386 [package=dip08]
  C5 = Ceramic Capacitor [capacitance="100 nF" voltage=35V package="1206 [SMD, multilayer]"]
  LED1 = smd LED [color="Red (633nm)" package="0805 [SMD]"]
  R1 = Resistor [tolerance=±5% resistance=220 package="2010 [SMD]"]

nets:
  N1: C1.-, U3.+IN
  N2: C1.+, TRS1.Ring, TRS1.Tip
  N3: C2.-, SP1.+
  N4: C2.+, U3.OUT
  N5: SP1.-, VCC1.-, TRS1.Sleeve, U3.-IN, U3.V-, C5.1, R1.Pin_1
  N6: VCC1.+, U3.V+, LED1.anode
  N7: U3.BP, C5.0
  N8: LED1.cathode, R1.Pin_0
