# Fritzing sketch SR-Latch (2 transistors) (saved by Fritzing 1.0.6)
circuit board: 8.46667cm x 5.64444cm
breadboards: 1

parts:
  Q1 = NPN-Transistor [package="TO92 [THT]"]
  Q2 = PNP-Transistor [package="TO92 [THT]"]
  R1 = Resistor [tolerance=±5% resistance=100k package="2512 [SMD]"]
  R2 = Resistor [tolerance=±5% resistance=10k package="2512 [SMD]"]
  S1 = SWITCH-MOMENTARY-2 [package=tactile-pth]
  S2 = SWITCH-MOMENTARY-2 [package=tactile-pth]
  LED1 = LED - 5mm [color="Green (570nm)" current=0.030A package="5 mm [THT]"]
  V1 = DC Power [voltage=5V]
  R7 = Resistor [tolerance=±5% resistance=100k package="2512 [SMD]"]
  R8 = Resistor [tolerance=±5% resistance=10k package="2512 [SMD]"]
  LED3 = LED - 5mm [color="Red (660nm)" current=0.030A package="5 mm [THT]"]
  R9 = Resistor [tolerance=±5% resistance=220 package="2512 [SMD]"]
  R10 = Resistor [tolerance=±5% resistance=220 package="2512 [SMD]"]

nets:
  GND: Q1.E, Q2.E, R9.Pin_1, R10.Pin_1
  N1: Q1.B, R1.Pin_0, S1.1
  N2: Q1.C, R2.Pin_0, LED1.anode, R7.Pin_0
  N3: Q2.B, R1.Pin_1, S2.1, R7.Pin_1
  N4: Q2.C, R8.Pin_0, LED3.anode
  N5: R2.Pin_1, V1.V+, R8.Pin_1
  N6: S1.2, S2.2, V1.V-
  N7: LED1.cathode, R9.Pin_0
  N8: LED3.cathode, R10.Pin_0
