# Fritzing sketch LED-Blinker (saved by Fritzing 1.0.5)
breadboards: 2

parts:
  R2 = Resistor [tolerance=±5% power=0.25W resistance=220 package=THT]
  Part1 = Arduino Uno (Rev3)
  LED5 = LED - 5mm [color="Red (633nm)" current=0.030A package="5 mm [THT]"]
  R4 = Resistor [tolerance=±5% power=0.25W resistance=220 package=THT]
  LED6 = LED - 5mm [color="Red (633nm)" current=0.030A package="5 mm [THT]"]
  R5 = Resistor [tolerance=±5% power=0.25W resistance=220 package=THT]
  LED7 = LED - 5mm [color="Red (633nm)" current=0.030A package="5 mm [THT]"]
  R6 = Resistor [tolerance=±5% power=0.25W resistance=220 package=THT]
  LED8 = LED - 5mm [color="Red (633nm)" current=0.030A package="5 mm [THT]"]
  R7 = Resistor [tolerance=±5% power=0.25W resistance=220 package=THT]
  LED9 = LED - 5mm [color="Red (633nm)" current=0.030A package="5 mm [THT]"]
  R8 = Resistor [tolerance=±5% power=0.25W resistance=220 package=THT]
  LED10 = LED - 5mm [color="Red (633nm)" current=0.030A package="5 mm [THT]"]
  R9 = Resistor [tolerance=±5% power=0.25W resistance=220 package=THT]
  LED11 = LED - 5mm [color="Red (633nm)" current=0.030A package="5 mm [THT]"]
  R10 = Resistor [tolerance=±5% power=0.25W resistance=220 package=THT]
  LED12 = LED - 5mm [color="Red (633nm)" current=0.030A package="5 mm [THT]"]
  R11 = Resistor [tolerance=±5% power=0.25W resistance=220 package=THT]  # not connected
  LED13 = LED - 5mm [color="Red (633nm)" current=0.030A package="5 mm [THT]"]  # not connected
  R12 = Resistor [tolerance=±5% power=0.25W resistance=220 package=THT]
  LED14 = LED - 5mm [color="Red (633nm)" current=0.030A package="5 mm [THT]"]
  BAT1 = BC9VPC [package=bc9vpc]
  VM1 = Multimeter (DC Voltage)
  VM2 = Multimeter (Ohmmeter)
  VM3 = Multimeter (DC Voltage)  # not connected
  R13 = Resistor [tolerance=±5% power=0.25W resistance=220 package=THT]
  BAT2 = BC9VPC [package=bc9vpc]
  VCC1 = Battery block 9V [internal_resistance=0.1Ω]  # not connected
  S1 = Toggle Switch [package=THT]  # not connected

nets:
  N1: R2.Pin_0, Part1.GND, R4.Pin_0, R5.Pin_0, R6.Pin_0, R7.Pin_0, R8.Pin_0, R9.Pin_0, R10.Pin_0, R12.Pin_0, BAT1.V-, VM1.COM_Probe, VM2.COM_Probe
  N2: R2.Pin_1, LED5.cathode
  N3: Part1.D8, LED10.anode
  N4: Part1.D9_PWM, LED9.anode
  N5: Part1.D10_PWM/SS, LED8.anode
  N6: Part1.D11_PWM/MOSI, LED7.anode
  N7: Part1.D12/MISO, LED6.anode
  N8: Part1.D13/SCK, LED5.anode
  N9: Part1.D5_PWM, LED14.anode
  N10: Part1.D6_PWM, LED12.anode
  N11: Part1.D7, LED11.anode
  N12: Part1.VIN, BAT1.V+, VM1.V_Probe
  N13: R4.Pin_1, LED6.cathode, VM2.V_Probe
  N14: R5.Pin_1, LED7.cathode
  N15: R6.Pin_1, LED8.cathode
  N16: R7.Pin_1, LED9.cathode
  N17: R8.Pin_1, LED10.cathode
  N18: R9.Pin_1, LED11.cathode
  N19: R10.Pin_1, LED12.cathode
  N20: R12.Pin_1, LED14.cathode
  N21: R13.Pin_0, BAT2.V-

notes:
  voltage
  Resistance

// code stored in the sketch: Sequential_blinking.ino


int leds[] = {13,12,11,10,9,8,7,6,5,4};
int count = 10; //i believe these two are global variables now

void setup()
{
  for (int i = 0; i < count; i++)
  {
    pinMode(leds[i], OUTPUT);
  }
}

void loop()
{
  for (int i =0; i < count; i++)
  {
    digitalWrite(leds[i], HIGH);
    delay(100);           //loop through each led and change state to high
  }

  for (int j = 0; j < count; j++)
  {
    digitalWrite(leds[j], LOW); //loop through each led but now change state to low
    delay(100);
  }
}
