# Fritzing sketch SR-Latch (saved by Fritzing 1.0.5)
breadboards: 1

parts:
  Q1 = NPN-Transistor [package="TO92 [THT]"]  # not connected
  Q2 = NPN-Transistor [package="TO92 [THT]"]  # not connected
  Q3 = NPN-Transistor [package="TO92 [THT]"]
  Q4 = NPN-Transistor [package="TO92 [THT]"]
  R1 = Resistor [tolerance=±5% resistance=10k package="2010 [SMD]"]
  R2 = Resistor [tolerance=±5% resistance=10k package="2010 [SMD]"]  # not connected
  R3 = Resistor [tolerance=±5% resistance=47k package="2010 [SMD]"]  # not connected
  R4 = Resistor [tolerance=±5% resistance=47k package="2010 [SMD]"]  # not connected
  R5 = Resistor [tolerance=±5% resistance=47k package="2010 [SMD]"]
  R6 = Resistor [tolerance=±5% resistance=47k package="2010 [SMD]"]
  Q5 = NPN-Transistor [package="TO92 [THT]"]
  Q6 = NPN-Transistor [package="TO92 [THT]"]  # not connected
  R7 = Resistor [tolerance=±5% resistance=10k package="2010 [SMD]"]
  R8 = Resistor [tolerance=±5% resistance=47k package="2010 [SMD]"]  # not connected
  R9 = Resistor [tolerance=±5% resistance=47k package="2010 [SMD]"]  # not connected

nets:
  N1: Q3.E, Q4.E, R7.Pin_0
  N2: Q3.B, R6.Pin_0
  N3: Q3.C, Q4.C, R1.Pin_1
  N4: Q4.B, R5.Pin_0
  N5: Q5.C, R7.Pin_1
