# Fritzing sketch led-arrays (saved by Fritzing 1.0.5)
circuit board: 8.46667cm x 5.64444cm
breadboards: 1

parts:
  Part1 = Arduino Uno (Rev3)
  LED1 = smd LED [color="Red (633nm)" package="1206 [SMD]"]
  R1 = Resistor [tolerance=±5% resistance=220 package="2512 [SMD]"]
  LED2 = smd LED [color="Red (633nm)" package="1206 [SMD]"]
  R2 = Resistor [tolerance=±5% resistance=220 package="2512 [SMD]"]
  LED3 = smd LED [color="Red (633nm)" package="1206 [SMD]"]
  R3 = Resistor [tolerance=±5% resistance=220 package="2512 [SMD]"]
  LED4 = smd LED [color="Red (633nm)" package="1206 [SMD]"]
  R4 = Resistor [tolerance=±5% resistance=220 package="2512 [SMD]"]
  LED5 = smd LED [color="Red (633nm)" package="1206 [SMD]"]
  R5 = Resistor [tolerance=±5% resistance=220 package="2512 [SMD]"]
  R6 = Resistor [tolerance=±5% resistance=220 package="2512 [SMD]"]
  LED6 = smd LED [color="Red (633nm)" package="1206 [SMD]"]
  BAT1 = BC9VPC [package=bc9vpc]

nets:
  N1: Part1.GND, R1.Pin_0, R2.Pin_0, R3.Pin_0, R4.Pin_0, R5.Pin_0, R6.Pin_0, BAT1.V-
  N2: Part1.D2, LED1.anode
  N3: Part1.D3_PWM, LED2.anode
  N4: Part1.D4, LED3.anode
  N5: Part1.D5_PWM, LED4.anode
  N6: Part1.D6_PWM, LED5.anode
  N7: Part1.D7, LED6.anode
  N8: Part1.VIN, BAT1.V+
  N9: LED1.cathode, R1.Pin_1
  N10: LED2.cathode, R2.Pin_1
  N11: LED3.cathode, R3.Pin_1
  N12: LED4.cathode, R4.Pin_1
  N13: LED5.cathode, R5.Pin_1
  N14: R6.Pin_1, LED6.cathode
