# Fritzing sketch Untitled momentary-switches (saved by Fritzing 1.0.5)
breadboards: 1

parts:
  R1 = Resistor [tolerance=±5% resistance=10k package="2512 [SMD]"]
  R2 = Resistor [tolerance=±5% resistance=10k package="2512 [SMD]"]
  LED1 = smd LED [color="White (4500K)" package="0805 [SMD]"]
  S1 = Momentary Switch [package=tactile-pth]
  Part1 = Arduino Uno (Rev3)
  LED2 = smd LED [color="White (4500K)" package="0805 [SMD]"]
  S2 = Momentary Switch [package=tactile-pth]
  R3 = Resistor [tolerance=±5% resistance=220 package="2512 [SMD]"]
  R4 = Resistor [tolerance=±5% resistance=220 package="2512 [SMD]"]

nets:
  N1: R1.Pin_0, R2.Pin_0, Part1.GND, R3.Pin_0, R4.Pin_0
  N2: R1.Pin_1, S1.3
  N3: R2.Pin_1, S2.3
  N4: LED1.cathode, R4.Pin_1
  N5: LED1.anode, Part1.D7
  N6: S1.2, Part1.D3_PWM
  N7: S1.4, Part1.5V, S2.4
  N8: Part1.D8, LED2.anode
  N9: Part1.D2, S2.2
  N10: LED2.cathode, R3.Pin_1
