# Fritzing sketch reaction-time-game (saved by Fritzing 1.0.5)
breadboards: 1

parts:
  Part1 = Arduino Uno (Rev3)
  LED1 = smd LED [color="Red (633nm)" package="1206 [SMD]"]
  R1 = Resistor [tolerance=±5% resistance=220 package="0603 [SMD]"]
  R2 = Resistor [tolerance=±5% resistance=10k package="0603 [SMD]"]
  S1 = Momentary Switch [package=tactile-pth]
  VCC1 = Battery block 9V [internal_resistance=0.1Ω]

nets:
  N1: Part1.D9_PWM, R2.Pin_1, S1.2
  N2: Part1.D10_PWM/SS, LED1.anode
  N3: Part1.GND, R1.Pin_1, R2.Pin_0, VCC1.-
  N4: Part1.5V, S1.1
  N5: Part1.VIN, VCC1.+
  N6: LED1.cathode, R1.Pin_0
