# Fritzing sketch rgb-led-potentiometers (saved by Fritzing 1.0.5)
circuit board: 8.46667cm x 5.64444cm
breadboards: 1

parts:
  Part1 = Arduino Uno (Rev3)
  GREEN_R2 = Rotary Potentiometer (Small) [maximum_resistance=100kΩ knob_status=50% power=0.5W package=THT]
  R2 = Resistor [tolerance=±5% resistance=220 package="0402 [SMD]"]
  RED_R1 = Rotary Potentiometer (Small) [maximum_resistance=100kΩ knob_status=50% power=0.5W package=THT]
  BLUE_R3 = Rotary Potentiometer (Small) [maximum_resistance=100kΩ knob_status=50% power=0.5W package=THT]
  LED3 = RGB LED (com. cathode, rgb) [color="Red (633nm)" current=0.030A package="5 mm [THT]"]
  R3 = Resistor [tolerance=±5% resistance=220 package="0402 [SMD]"]
  R4 = Resistor [tolerance=±5% resistance=220 package="0402 [SMD]"]

nets:
  N1: Part1.A0, RED_R1.wiper
  N2: Part1.A1, GREEN_R2.wiper
  N3: Part1.A2, BLUE_R3.wiper
  N4: Part1.D9_PWM, R2.Pin_0
  N5: Part1.D10_PWM/SS, R3.Pin_0
  N6: Part1.D11_PWM/MOSI, R4.Pin_0
  N7: Part1.GND, GREEN_R2.leg1, RED_R1.leg1, BLUE_R3.leg1, LED3.common_cathode
  N8: Part1.5V, GREEN_R2.leg2, RED_R1.leg2, BLUE_R3.leg2
  N9: R2.Pin_1, LED3.red_anode
  N10: LED3.green_anode, R3.Pin_1
  N11: LED3.blue_anode, R4.Pin_1
