# Fritzing sketch rgb-led (saved by Fritzing 1.0.5)
breadboards: 1

parts:
  LED1 = RGB LED - (4 legs) [color="Red (633nm)" current=30mA package="5 mm [THT]"]
  Part1 = Arduino Uno (Rev3)
  R1 = Resistor [tolerance=±5% resistance=220 package="0603 [SMD]"]
  R2 = Resistor [tolerance=±5% resistance=220 package="0603 [SMD]"]
  R3 = Resistor [tolerance=±5% resistance=220 package="0603 [SMD]"]
  BAT1 = BC9VPC [package=bc9vpc]
  RED = SWITCH-MOMENTARY-2 [package=tactile-pth]
  GREEN = SWITCH-MOMENTARY-2 [package=tactile-pth]
  BLUE = SWITCH-MOMENTARY-2 [package=tactile-pth]
  R5 = Resistor [tolerance=±5% resistance=10k package="0603 [SMD]"]
  R6 = Resistor [tolerance=±5% resistance=10k package="0603 [SMD]"]
  R7 = Resistor [tolerance=±5% resistance=10k package="0603 [SMD]"]

nets:
  N1: LED1.red_cathode, R1.Pin_1
  N2: LED1.common_anode, Part1.5V, RED.2, GREEN.2, BLUE.2
  N3: LED1.green_cathode, R2.Pin_1
  N4: LED1.blue_cathode, R3.Pin_1
  N5: Part1.D9_PWM, R1.Pin_0
  N6: Part1.D10_PWM/SS, R2.Pin_0
  N7: Part1.D11_PWM/MOSI, R3.Pin_0
  N8: Part1.D12/MISO, R7.Pin_1
  N9: Part1.D2, R5.Pin_1
  N10: Part1.D3_PWM, R6.Pin_1
  N11: Part1.GND, BAT1.V-
  N12: Part1.VIN, BAT1.V+
  N13: RED.1, R5.Pin_0
  N14: GREEN.1, R6.Pin_0
  N15: BLUE.1, R7.Pin_0
