# Fritzing sketch traffic-light (saved by Fritzing 1.0.5)
breadboards: 1

parts:
  R3 = Resistor [tolerance=±5% power=0.25W resistance=220 package=THT]
  R4 = Resistor [tolerance=±5% power=0.25W resistance=1k package=THT]
  LED2 = smd LED [color="Red (633nm)" package="1206 [SMD]"]
  R5 = PHOTOCELL [package=photocell]
  Part1 = Arduino Uno (Rev3)
  R6 = Resistor [tolerance=±5% power=0.25W resistance=220 package=THT]
  LED4 = smd LED [color="Yellow (595nm)" package="1206 [SMD]"]
  R7 = Resistor [tolerance=±5% power=0.25W resistance=220 package=THT]
  LED5 = smd LED [color="Green (555nm)" package="1206 [SMD]"]

nets:
  N1: R3.Pin_0, R4.Pin_0, Part1.GND, R6.Pin_0, R7.Pin_0
  N2: R3.Pin_1, LED2.cathode
  N3: R4.Pin_1, R5.P$1, Part1.A0
  N4: LED2.anode, Part1.D3_PWM
  N5: R5.P$2, Part1.5V
  N6: Part1.D5_PWM, LED4.anode
  N7: Part1.D6_PWM, LED5.anode
  N8: R6.Pin_1, LED4.cathode
  N9: R7.Pin_1, LED5.cathode
