# Fritzing sketch DHT11-Temperature (saved by Fritzing 1.0.5)
breadboards: 1

parts:
  LCD = LCD1602-I2C
  Part2 = Arduino Uno (Rev3)
  DHT11 = Humidity and Temperature Sensor RHT03

nets:
  GND: LCD.GND, Part2.GND, DHT11.GND_1
  VCC: LCD.VCC, Part2.5V, DHT11.Vcc
  N1: LCD.SDA, Part2.A4/SDA
  N2: LCD.SCL, Part2.A5/SCL
  N3: Part2.D2, DHT11.Data-signal

notes:
  DHT11
  Facing the block side:
  1- DATA
  2- VCC
  3- GND

custom parts:
  LCD1602-I2C: A standard character display, usually with 2x16 characters. Comes in many colors with LCM1602 IIC attached.
