# Fritzing sketch infrared-sensors (saved by Fritzing 1.0.5)
breadboards: 1

parts:
  R1 = Resistor [tolerance=±5% power=0.25W resistance=220 package=THT]
  R2 = Resistor [tolerance=±5% power=0.25W resistance=220 package=THT]
  LED1 = smd LED [color="Green (565nm)" package="0805 [SMD]"]
  LED2 = smd LED [color="Blue (430nm)" package="0805 [SMD]"]
  LED3 = smd LED [color="White (4500K)" package="0805 [SMD]"]
  LED4 = smd LED [color="Red (633nm)" package="0805 [SMD]"]
  R3 = Resistor [tolerance=±5% power=0.25W resistance=220 package=THT]
  R4 = Resistor [tolerance=±5% power=0.25W resistance=220 package=THT]
  Part1 = Arduino Uno (Rev3)
  IR1 = TSOP312.., 314.. [package=THT]

nets:
  N1: R1.Pin_0, R2.Pin_0, R3.Pin_0, R4.Pin_0, Part1.5V, IR1.Vs
  N2: R1.Pin_1, LED1.anode
  N3: R2.Pin_1, LED3.cathode
  N4: LED1.cathode, Part1.D7
  N5: LED2.cathode, R3.Pin_1
  N6: LED2.anode, Part1.D5_PWM
  N7: LED3.anode, Part1.D6_PWM
  N8: LED4.cathode, R4.Pin_1
  N9: LED4.anode, Part1.D4
  N10: Part1.D9_PWM, IR1.Data
  GND: Part1.GND, IR1.GND
