# Fritzing sketch ultrasonic-distance (saved by Fritzing 1.0.5)
breadboards: 1

parts:
  LCD = LCD1602-I2C
  Part2 = Arduino Uno (Rev3)
  BUZZER = Passive Buzzer
  HC-SR04_Sensor_1 = HC-SR04 Ultrasonic Distance Sensor
  R1 = Resistor [tolerance=±5% resistance=220 package="0402 [SMD]"]

nets:
  GND: LCD.GND, Part2.GND, HC-SR04_Sensor_1.GND, R1.Pin_0
  VCC: LCD.VCC, Part2.5V, HC-SR04_Sensor_1.VCC
  N1: LCD.SDA, Part2.A4/SDA
  N2: LCD.SCL, Part2.A5/SCL
  N3: Part2.D8, BUZZER.S
  N4: Part2.D9_PWM, HC-SR04_Sensor_1.TRIG
  N5: Part2.D10_PWM/SS, HC-SR04_Sensor_1.ECHO
  N6: BUZZER.-, R1.Pin_1

custom parts:
  LCD1602-I2C: A standard character display, usually with 2x16 characters. Comes in many colors with LCM1602 IIC attached.
