# Fritzing sketch working-with-google-assistant-schema (saved by Fritzing 1.0.6)
breadboards: 2

parts:
  M1 = DOIT Esp32 DevKit v1 (30 pins long, 11 pins width) [part_number=ESP32S-PIN30]
  LED1 = smd LED [color="White (4500K)" package="0805 [SMD]"]
  LED2 = smd LED [color="White (4500K)" package="0805 [SMD]"]
  LED3 = smd LED [color="White (4500K)" package="0805 [SMD]"]
  LED4 = smd LED [color="White (4500K)" package="0805 [SMD]"]
  LED5 = smd LED [color="White (4500K)" package="0805 [SMD]"]
  LED6 = smd LED [color="White (4500K)" package="0805 [SMD]"]
  LED7 = smd LED [color="White (4500K)" package="0805 [SMD]"]
  LED8 = smd LED [color="White (4500K)" package="0805 [SMD]"]
  LED10 = smd LED [color="White (4500K)" package="0805 [SMD]"]
  LED11 = smd LED [color="White (4500K)" package="0805 [SMD]"]
  R1 = Resistor [tolerance=±5% resistance=220 package="1206 [SMD]"]
  R2 = Resistor [tolerance=±5% resistance=220 package="1206 [SMD]"]
  R3 = Resistor [tolerance=±5% resistance=220 package="1206 [SMD]"]
  R4 = Resistor [tolerance=±5% resistance=220 package="1206 [SMD]"]
  R5 = Resistor [tolerance=±5% resistance=220 package="1206 [SMD]"]
  R6 = Resistor [tolerance=±5% resistance=220 package="1206 [SMD]"]
  R7 = Resistor [tolerance=±5% resistance=220 package="1206 [SMD]"]
  R8 = Resistor [tolerance=±5% resistance=220 package="1206 [SMD]"]
  R9 = Resistor [tolerance=±5% resistance=220 package="1206 [SMD]"]
  R10 = Resistor [tolerance=±5% resistance=220 package="1206 [SMD]"]

nets:
  GND: M1.GND, R1.Pin_0, R2.Pin_0, R3.Pin_0, R4.Pin_1, R5.Pin_1, R6.Pin_1, R7.Pin_1, R8.Pin_1, R9.Pin_1, R10.Pin_1
  N1: M1.D15, LED5.anode
  N2: M1.D2, LED4.anode
  N3: M1.D4, LED3.anode
  N4: M1.D5, LED2.anode
  N5: M1.D18, LED1.anode
  N6: M1.D19, LED6.anode
  N7: M1.D23, LED7.anode
  N8: M1.D14, LED10.anode
  N9: M1.D12, LED11.anode
  N10: M1.D13, LED8.anode
  N11: LED1.cathode, R8.Pin_0
  N12: LED2.cathode, R7.Pin_0
  N13: LED3.cathode, R6.Pin_0
  N14: LED4.cathode, R5.Pin_0
  N15: LED5.cathode, R4.Pin_0
  N16: LED6.cathode, R9.Pin_0
  N17: LED7.cathode, R10.Pin_0
  N18: LED8.cathode, R3.Pin_1
  N19: LED10.cathode, R1.Pin_1
  N20: LED11.cathode, R2.Pin_1

custom parts:
  DOIT Esp32 DevKit v1 (30 pins long, 11 pins width): The DOIT Esp32 DevKit v1 is one of the development board created by DOIT to evaluate the ESP-WROOM-32 module. It is based on the ESP32 microcontroller that boasts Wifi, Bluetooth, Ethernet and Low Power support all in a single chip. (vanepp) made breadboard work, adjusted pin numbering and labels and reduced size of schematic and cleaned up pcb. This chip is 30pins long (2 x15) and 11 pins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
